# Fritzing sketch FoodDetector (saved by Fritzing 0.9.3b)
breadboards: 1

parts:
  BT1 = Bluetooth HC-06u [package=THT]
  Componente1 = Arduino Uno (Rev3)
  R1 = Resistor [tolerance=±5% resistance=220k package=THT]

nets:
  VCC: BT1.VCC, Componente1.5V
  GND: BT1.GND, Componente1.GND, R1.Pin_0
  N1: BT1.TXD, Componente1.D10_PWM/SS
  N2: BT1.RXD, Componente1.D11_PWM/MOSI
  N3: Componente1.A0, R1.Pin_1

custom parts:
  Bluetooth HC-06u: Bluetooth HC-06 - face up, pins down 16.5mm x 37.5mm PCB
