# Fritzing sketch EsquematicoGafas (saved by Fritzing 0.9.2b)
breadboards: 1

parts:
  Parte2 = SRF05 Ultrasonic Rangefinder
  R1 = Resistor [tolerance=±5% resistance=220 package="0603 [SMD]"]
  S1 = Momentary Switch [package=ksa_sealed_tac_switch]
  R2 = Resistor [tolerance=±5% resistance=10k package="0603 [SMD]"]
  Parte3 = Arduino Micro (Rev3)
  LED1 = LED - 3mm [color="Green (555nm)" package="3 mm [THT]"]
  J1 = Piezo Speaker
  VCC1 = Battery block 9V

nets:
  VCC: Parte2.VCC, S1.4, Parte3.5V
  N1: Parte2.Trig, Parte3.D11_PWM
  N2: Parte2.Echo, Parte3.D12_PWM/A11
  GND: Parte2.GND, R2.Pin_0, Parte3.GND, LED1.cathode, J1.pin1, VCC1.-
  N3: R1.Pin_0, LED1.anode
  N4: R1.Pin_1, Parte3.D5_PWM
  N5: S1.1, R2.Pin_1, Parte3.D2/SDA
  N6: Parte3.D6_PWM/A7, J1.pin2
  N7: Parte3.VIN, VCC1.+
