# Fritzing sketch EsquemaVehiculo (saved by Fritzing 0.9.2b)
breadboards: 2

parts:
  BAT1 = 18650 battery holder [part_number=3,7v package=battery-18650-kit]
  BAT2 = 18650 battery holder [package=battery-18650-kit]
  M3 = DC Motor
  M4 = DC Motor
  M5 = DC Motor
  M6 = DC Motor
  Parte2 = Rotoshield - Motor driver shield for Arduino
  BT1 = Bluetooth HC-06u [package=THT]

nets:
  VIN: BAT1.+, Parte2.VIN, Parte2.VCC
  N1: BAT1.-, BAT2.+
  GND: BAT2.-, Parte2.GND, BT1.GND
  N2: M3.pin_1, Parte2.M3-2
  N3: M3.pin_2, Parte2.M3-1
  N4: M4.pin_1, Parte2.M4-1
  N5: M4.pin_2, Parte2.M4-2
  N6: M5.pin_1, Parte2.M1-1
  N7: M5.pin_2, Parte2.M1-2
  N8: M6.pin_1, Parte2.M2-1
  N9: M6.pin_2, Parte2.M2-2
  N10: Parte2.DIG_10, BT1.TXD
  N11: Parte2.DIG_11, BT1.RXD
  +5V: Parte2.+5V, BT1.VCC

custom parts:
  18650 battery holder: 18650 Battery Holder
  Bluetooth HC-06u: Bluetooth HC-06 - face up, pins down 16.5mm x 37.5mm PCB
